# Fritzing sketch breadboard_hasco2014 (saved by Fritzing 0.8.7b)
breadboards: 1

parts:
  R1 = Resistor [tolerance=±5% resistance=220 package=THT]
  Componente1 = Arduino Uno (Rev3)
  P1 = S1133 Si Photodiode [package="8mm Ceramic [THT]"]
  R2 = Resistor [tolerance=±5% resistance=220 package=THT]
  R3 = Temperature Sensor (Thermistor) [thermistor_type=NTC package=THT]

nets:
  N1: R1.Pin_0, Componente1.GND, P1.cathode, R3.pin_1
  N2: R1.Pin_1, Componente1.A0, P1.anode
  N3: Componente1.A5/SCL, R2.Pin_1, R3.pin_0
